# Fritzing sketch Skematik (saved by Fritzing 0.9.9b)
breadboards: 1

parts:
  RELAY_1_CHANNEL = KY-019 5V Relay Module [package="Breakout board"]
  RFID_READER = RFID-RC522-v2
  ARDUINO_UNO = Arduino Uno (Rev3)
  BATTERY_3_SLOT = 4 x AAA Battery Mount
  LCD_WITH_I2C = LCD1602-I2C
  PUSH_BUTTON = Round Pushbutton
  BUZZER = Piezo Speaker
  SOLENOID_LOCK = uhppote-electric-strike-door-lock_1

nets:
  N1: RELAY_1_CHANNEL.S, ARDUINO_UNO.D7
  5V: RELAY_1_CHANNEL.+, ARDUINO_UNO.5V, LCD_WITH_I2C.VCC
  GND: RELAY_1_CHANNEL.-, RFID_READER.GND, ARDUINO_UNO.GND, BATTERY_3_SLOT.-, LCD_WITH_I2C.GND, PUSH_BUTTON.leg1, BUZZER.pin1
  N2: RELAY_1_CHANNEL.NO, SOLENOID_LOCK.connector1
  N3: RFID_READER.SDA, ARDUINO_UNO.D10_PWM/SS
  N4: RFID_READER.SCK, ARDUINO_UNO.D13/SCK
  N5: RFID_READER.MOSI, ARDUINO_UNO.D11_PWM/MOSI
  N6: RFID_READER.MISO, ARDUINO_UNO.D12/MISO
  N7: RFID_READER.RST, ARDUINO_UNO.D9_PWM
  3.3V: RFID_READER.3.3V, ARDUINO_UNO.3V3
  N8: ARDUINO_UNO.A4/SDA, LCD_WITH_I2C.SDA
  N9: ARDUINO_UNO.A5/SCL, LCD_WITH_I2C.SCL
  N10: ARDUINO_UNO.D8, BUZZER.pin2
  N11: ARDUINO_UNO.D2, PUSH_BUTTON.leg0
  N12: ARDUINO_UNO.VIN, BATTERY_3_SLOT.+

notes:
  RFID MODULE
  SDA D10
  SCK D13
  MOSI D11
  MISO D12
  GND GND
  RST D9
  3.3 V KE 3.3V
  RELAY
  IN D7
  VCC 5V
  GND GND
  - NO KE SLOCK
  - COM KE GND BATERAI
  PUSH BUTTON
  (INPUT PULL-UP)
  D2 & GND
  LCD I2C
  SDA A4
  SCL A5
  VCC 5V
  GND GND
  BUZZER
  + D8
  - GND
  SOLENOID LOCK
  - 1 KE NO (NORMALY OPEN) RELAY
  - 1 KE VCC BATERAI HOLDER
  POWER
  + KE VIN ARDUINO
  - KE GND ARDUINO

custom parts:
  KY-019 5V Relay Module: KY-019 5V Relay module, used to control AC circuits. (Special thanks to vanepp for fixing the PCB holes and other errors)
  RFID-RC522-v2: A simple China made RFID-RC522 Reader; do check the pin labels, as this is a MFRC522 based clone.
  LCD1602-I2C: A standard character display, usually with 2x16 characters. Comes in many colors with LCM1602 IIC attached.
